# Fritzing sketch tinyroaster (saved by Fritzing 0.9.3b)
circuit board: 8.46667cm x 5.64444cm
stripboards: 1

parts:
  U1 = attiny85 [package=dip]
  LCD1 = LCD screen
  Q1 = Basic FET N-Channel [package="TO220 [THT]"]
  R3 = Rotary Potentiometer (Small) [maximum_resistance=100kΩ package=THT]
  R4 = Resistor [tolerance=±5% resistance=10k package=THT]
  R5 = Resistor [tolerance=±5% resistance=40k package=THT]
  U3 = Voltage Regulator - 5V [package="DPak [SMD]"]
  J1 = Power Jack [package=power_jack_combo]
  U4 = MAX6675 [package=so08]
  C1 = Electrolytic Capacitor [capacitance=100μF voltage=20V package="0807 [SMD, electrolytic]"]
  C2 = Electrolytic Capacitor [capacitance=47µF voltage=20V package="0807 [SMD, electrolytic]"]
  74HC4 = 74HC164 [package="DIP (Dual Inline) [THT]"]
  R6 = TRIMPOT [package=trim_pot_pth]
  D2 = Diode [package=diode-1n4148]
  R7 = Resistor [tolerance=±5% resistance=1k package=THT]

nets:
  GND: U1.Pin_2, U1.Pin_3, U1.Pin_4, LCD1.VSS, LCD1.R/W, Q1.gate, U3.GND, J1.GND, U4.SCK, U4.CS, U4.MISO, C1.-, C2.-, 74HC4.GND
  VDD: U1.Pin_8, LCD1.VDD, U3.output_voltage, C1.+, 74HC4.CLR, 74HC4.VCC, R6.CCW
  N1: LCD1.V0, R6.WIPER
  N2: LCD1.RS, 74HC4.QC
  N3: LCD1.E, D2.A, R7.Pin_1
  N4: LCD1.DB4, 74HC4.QD
  N5: LCD1.DB5, 74HC4.QE
  N6: LCD1.DB6, 74HC4.QF
  N7: LCD1.DB7, 74HC4.QG
  N8: Q1.drain, Q1.source, U3.input_voltage, J1.PWR, C2.+
  N9: R3.leg1, R4.Pin_1
  N10: R3.leg2, R5.Pin_1
  N11: R4.Pin_0, U4.VSS, 74HC4.QA
  N12: R5.Pin_0, 74HC4.A, 74HC4.B, R7.Pin_0
  N13: 74HC4.QH, D2.C

notes:
  18-20V

custom parts:
  74HC164: 8-Bit Parallel-Out Serial Shift Registers
